// Logisim project lab2-update.circ as structural Verilog: 1 circuit, main circuit main
module main (
  input  [7:0] A,
  input  [7:0] DATA,
  input  [7:0] B,
  input  [1:0] ADDR,
  input  [1:0] in_5,
  input  [7:0] _1,
  input  E,
  input  [2:0] in_8,
  output [7:0] out_9,
  output [7:0] out_10
);

  wire CLK_out, decoder_1_out0, decoder_1_out1, decoder_1_out2;
  wire [7:0] adder_1_out, adder_2_out, and_1_out, not_1_out, or_1_out, register_1_q, register_2_q,
       register_3_q, register_4_q, subtractor_1_out, subtractor_2_out, xor_1_out;

  assign not_1_out = ~A;  // NOT_Gate not_1, 8 bits wide
  Adder adder_1 (.a(A), .b(B), .out(adder_1_out));  // open: cin, cout
  Adder adder_2 (.a(A), .b(_1), .out(adder_2_out));  // open: cin, cout
  Subtractor subtractor_1 (.a(A), .b(B), .out(subtractor_1_out));  // open: bin, bout
  Subtractor subtractor_2 (.a(A), .b(_1), .out(subtractor_2_out));  // open: bin, bout
  assign and_1_out = A & B;  // AND_Gate and_1, 8 bits wide
  assign or_1_out = A | B;  // OR_Gate or_1, 8 bits wide
  assign xor_1_out = A ^ B;  // XOR_Gate xor_1, 8 bits wide
  Multiplexer #(.select(3), .width(8), .disabled(0)) multiplexer_1 (
    .in0(adder_1_out), .in1(adder_2_out), .in2(subtractor_1_out), .in3(subtractor_2_out), .in4(and_1_out),
    .in5(or_1_out), .in6(not_1_out), .in7(xor_1_out), .out(out_10), .sel(in_8));  // open: en
  Decoder #(.select(2), .disabled(0)) decoder_1 (
    .out0(decoder_1_out0), .out1(decoder_1_out1), .out2(decoder_1_out2), .out3(decoder_1_out2), .sel(ADDR),
    .en(E));
  Clock CLK (.out(CLK_out));
  Register register_1 (.D(DATA), .en(decoder_1_out0), .Q(register_1_q), .clk(CLK_out));  // open: clr
  Register register_2 (.D(DATA), .en(decoder_1_out1), .Q(register_2_q), .clk(CLK_out));  // open: clr
  Register register_3 (.D(DATA), .en(decoder_1_out2), .Q(register_3_q), .clk(CLK_out));  // open: clr
  Register register_4 (.D(DATA), .en(decoder_1_out2), .Q(register_4_q), .clk(CLK_out));  // open: clr
  Multiplexer #(.select(2), .width(8)) multiplexer_2 (
    .in0(register_1_q), .in1(register_2_q), .in2(register_3_q), .in3(register_4_q), .out(out_9), .sel(in_5));  // open: en
endmodule
